// Logisim project circ1.circ as structural Verilog: 1 circuit, main circuit main
module main (
  input  A,
  input  B,
  output C
);

  wire not_1_out;

  not not_1 (not_1_out, A);
  or or_1 (C, not_1_out, B);
endmodule
