// Logisim project regfile.circ as structural Verilog: 1 circuit, main circuit main
module main (
  input  [4:0] rs1,
  input  [4:0] rs2,
  input  [4:0] rd,
  input  [31:0] Write_Data,
  input  RegWEn,
  input  clk,
  output [31:0] ra,
  output [31:0] sp,
  output [31:0] t0,
  output [31:0] t1,
  output [31:0] t2,
  output [31:0] s0,
  output [31:0] s1,
  output [31:0] a0,
  output [31:0] Read_Data_1,
  output [31:0] Read_Data_2
);

  wire and_1_out, demultiplexer_1_out0, demultiplexer_1_out1, demultiplexer_1_out2, demultiplexer_1_out3,
       demultiplexer_1_out4, demultiplexer_1_out5, demultiplexer_1_out6, demultiplexer_1_out7,
       demultiplexer_1_out8, demultiplexer_1_out9, demultiplexer_1_out10, Reg0, Reg1, Reg2, Reg3, Reg4, Reg5,
       Reg6, Reg7, Reg8, Reg9, Reg10;
  wire [3:0] bit_extender_1_out, bit_extender_2_out, bit_extender_3_out;
  wire [31:0] out_0, out_3, out_4;

  Bit_Extender #(.in_width(5), .out_width(4)) bit_extender_1 (.in(rd), .out(bit_extender_1_out));
  Demultiplexer #(.select(4), .enable("false")) demultiplexer_1 (
    .out0(demultiplexer_1_out0), .out1(demultiplexer_1_out1), .out2(demultiplexer_1_out2),
    .out3(demultiplexer_1_out3), .out4(demultiplexer_1_out4), .out5(demultiplexer_1_out5),
    .out6(demultiplexer_1_out6), .out7(demultiplexer_1_out7), .out8(demultiplexer_1_out8),
    .out9(demultiplexer_1_out9), .out10(demultiplexer_1_out10), .in(1'b1), .sel(bit_extender_1_out));  // open: out11, out12, out13, out14, out15
  Register #(.width(32)) x0 (.D(Write_Data), .en(and_1_out), .clk(clk), .Q(out_0));  // open: clr
  and and_1 (and_1_out, 1'b0, Reg0);
  Register #(.width(32)) x1 (.D(Write_Data), .en(Reg1), .clk(clk), .Q(ra));  // open: clr
  Register #(.width(32)) x2 (.D(Write_Data), .en(Reg2), .clk(clk), .Q(sp));  // open: clr
  Register #(.width(32)) x5 (.D(Write_Data), .en(Reg5), .clk(clk), .Q(t0));  // open: clr
  Register #(.width(32)) x6 (.D(Write_Data), .en(Reg6), .clk(clk), .Q(t1));  // open: clr
  Register #(.width(32)) x7 (.D(Write_Data), .en(Reg7), .clk(clk), .Q(t2));  // open: clr
  Register #(.width(32)) x8 (.D(Write_Data), .en(Reg8), .clk(clk), .Q(s0));  // open: clr
  Register #(.width(32)) x9 (.D(Write_Data), .en(Reg9), .clk(clk), .Q(s1));  // open: clr
  Register #(.width(32)) x10 (.D(Write_Data), .en(Reg10), .clk(clk), .Q(a0));  // open: clr
  and and_2 (Reg0, demultiplexer_1_out0, RegWEn);
  and and_3 (Reg1, demultiplexer_1_out1, RegWEn);
  and and_4 (Reg2, demultiplexer_1_out2, RegWEn);
  and and_5 (Reg3, demultiplexer_1_out3, RegWEn);
  and and_6 (Reg4, demultiplexer_1_out4, RegWEn);
  and and_7 (Reg5, demultiplexer_1_out5, RegWEn);
  and and_8 (Reg6, demultiplexer_1_out6, RegWEn);
  and and_9 (Reg7, demultiplexer_1_out7, RegWEn);
  and and_10 (Reg8, demultiplexer_1_out8, RegWEn);
  and and_11 (Reg9, demultiplexer_1_out9, RegWEn);
  and and_12 (Reg10, demultiplexer_1_out10, RegWEn);
  Multiplexer #(.select(4), .width(32), .enable("false")) multiplexer_1 (
    .in0(out_0), .in1(ra), .in2(sp), .in3(out_3), .in4(out_4), .in5(t0), .in6(t1), .in7(t2), .in8(s0),
    .in9(s1), .in10(a0), .out(Read_Data_1), .sel(bit_extender_2_out));  // open: in11, in12, in13, in14, in15
  Multiplexer #(.select(4), .width(32), .enable("false")) multiplexer_2 (
    .in0(out_0), .in1(ra), .in2(sp), .in3(out_3), .in4(out_4), .in5(t0), .in6(t1), .in7(t2), .in8(s0),
    .in9(s1), .in10(a0), .out(Read_Data_2), .sel(bit_extender_3_out));  // open: in11, in12, in13, in14, in15
  Bit_Extender #(.in_width(5), .out_width(4)) bit_extender_2 (.in(rs1), .out(bit_extender_2_out));
  Bit_Extender #(.in_width(5), .out_width(4)) bit_extender_3 (.in(rs2), .out(bit_extender_3_out));

  // Other names for the same wires on the sheet: out_1[31:0] = ra; out_2[31:0] = sp; out_5[31:0] = t0;
  //   out_6[31:0] = t1; out_7[31:0] = t2; out_8[31:0] = s0; out_9[31:0] = s1; out_10[31:0] = a0;
  //   read_data1[31:0] = Read_Data_1; read_data2[31:0] = Read_Data_2; read_reg1[4:0] = rs1; read_reg2[4:0] = rs2;
  //   write_en = RegWEn; write_reg[4:0] = rd

  // Notes on the sheet:
  //   INPUTS to your circuit
  //   DON'T CHANGE THE LOCATIONS OF THE INPUTS AND OUTPUTS!
  //   These are DEBUG/TEST outputs from your circuit.
  //   OUTPUTS from your circuit
endmodule
