// Logisim project alu.circ as structural Verilog: 1 circuit, main circuit alu
module alu (
  input  [31:0] A,
  input  [31:0] B,
  input  [3:0] ALUSel,
  output [31:0] Result
);

  wire C_out, comparator_1_eq, comparator_2_lt, xor_2_out, xor_3_out;
  wire [4:0] bit_extender_1_out, bit_extender_2_out, bit_extender_3_out;
  wire [5:0] adder_2_out, bitadder_1_out, bitadder_2_out;
  wire [31:0] adder_4_out, ALU_ADD, ALU_AND, ALU_CNTO, ALU_DIV, ALU_DIVU, ALU_MULH, ALU_MULHU, ALU_MULT,
       ALU_OR, ALU_REMU, ALU_SIR, ALU_SLL, ALU_SLT, ALU_SRA, ALU_SRL, ALU_SUB, ALU_XOR, bit_extender_7_out,
       divider_2_out, LOW32, multiplexer_1_out, multiplexer_3_out, multiplexer_4_out, multiplexer_5_out,
       multiplier_2_cout, negator_1_out, negator_2_out, negator_3_out, negator_4_out, negator_5_out,
       not_1_out, not_2_out;

  assign ALU_AND = A & B;  // AND_Gate and_1, 32 bits wide
  Bit_Extender #(.in_width(32), .out_width(5), .\type ("zero")) bit_extender_1 (.in(B), .out(bit_extender_1_out));
  Bit_Extender #(.in_width(32), .out_width(5), .\type ("zero")) bit_extender_2 (.in(B), .out(bit_extender_2_out));
  assign ALU_XOR = A ^ B;  // XOR_Gate xor_1, 32 bits wide
  Subtractor #(.width(32)) subtractor_1 (.a(A), .b(B), .out(ALU_SUB));  // open: bin, bout
  Divider #(.width(32)) divider_1 (.a(A), .b(B), .out(ALU_DIVU), .rem(ALU_REMU));  // open: upper
  Shifter #(.width(32), .shift("ar")) shifter_1 (.in(A), .\dist (bit_extender_1_out), .out(ALU_SRA));
  Shifter #(.width(32)) shifter_2 (.in(A), .\dist (bit_extender_2_out), .out(ALU_SLL));
  Bit_Extender #(.in_width(32), .out_width(5), .\type ("zero")) bit_extender_3 (.in(B), .out(bit_extender_3_out));
  Comparator #(.width(32)) comparator_1 (
    .a({A[0], A[1], A[2], A[3], A[4], A[5], A[6], A[7], A[8], A[9], A[10], A[11], A[12], A[13], A[14], A[15], A[16], A[17], A[18], A[19], A[20], A[21], A[22], A[23], A[24], A[25], A[26], A[27], A[28], A[29], A[30], A[31]}),
    .b(B), .eq(comparator_1_eq));  // open: gt, lt
  assign ALU_OR = A | B;  // OR_Gate or_1, 32 bits wide
  Adder #(.width(32)) adder_1 (.a(A), .b(B), .out(ALU_ADD));  // open: cin, cout
  Multiplier #(.width(32)) multiplier_1 (.a(A), .b(B), .out(ALU_MULT), .cout(ALU_MULHU));  // open: cin
  Shifter #(.width(32), .shift("lr")) shifter_3 (.in(A), .\dist (bit_extender_3_out), .out(ALU_SRL));
  Comparator #(.width(32)) comparator_2 (.a(A), .b(B), .lt(comparator_2_lt));  // open: gt, eq
  assign ALU_SIR = {{31{1'b0}}, comparator_1_eq};  // Bit_Extender bit_extender_4
  assign ALU_SLT = {{31{1'b0}}, comparator_2_lt};  // Bit_Extender bit_extender_5
  BitAdder #(.width(1)) bitadder_1 (
    .in0(A[0]), .in1(A[1]), .in2(A[2]), .in3(A[3]), .in4(A[4]), .in5(A[5]), .in6(A[6]), .in7(A[7]),
    .in8(A[8]), .in9(A[9]), .in10(A[10]), .in11(A[11]), .in12(A[12]), .in13(A[13]), .in14(A[14]),
    .in15(A[15]), .in16(A[16]), .in17(A[17]), .in18(A[18]), .in19(A[19]), .in20(A[20]), .in21(A[21]),
    .in22(A[22]), .in23(A[23]), .in24(A[24]), .in25(A[25]), .in26(A[26]), .in27(A[27]), .in28(A[28]),
    .in29(A[29]), .in30(A[30]), .in31(A[31]), .out(bitadder_1_out));
  BitAdder #(.width(1)) bitadder_2 (
    .in0(B[0]), .in1(B[1]), .in2(B[2]), .in3(B[3]), .in4(B[4]), .in5(B[5]), .in6(B[6]), .in7(B[7]),
    .in8(B[8]), .in9(B[9]), .in10(B[10]), .in11(B[11]), .in12(B[12]), .in13(B[13]), .in14(B[14]),
    .in15(B[15]), .in16(B[16]), .in17(B[17]), .in18(B[18]), .in19(B[19]), .in20(B[20]), .in21(B[21]),
    .in22(B[22]), .in23(B[23]), .in24(B[24]), .in25(B[25]), .in26(B[26]), .in27(B[27]), .in28(B[28]),
    .in29(B[29]), .in30(B[30]), .in31(B[31]), .out(bitadder_2_out));
  Adder #(.width(6)) adder_2 (.a(bitadder_1_out), .b(bitadder_2_out), .out(adder_2_out));  // open: cin, cout
  assign ALU_CNTO = {{26{1'b0}}, adder_2_out};  // Bit_Extender bit_extender_6
  Multiplexer #(.width(32), .enable("false")) multiplexer_1 (
    .in0(A), .in1(negator_1_out), .out(multiplexer_1_out), .sel(A[31]));
  Negator #(.width(32)) negator_1 (.in(A), .out(negator_1_out));
  Negator #(.width(32)) negator_2 (.in(B), .out(negator_2_out));
  Negator #(.width(32)) negator_3 (.in(A), .out(negator_3_out));
  Negator #(.width(32)) negator_4 (.in(B), .out(negator_4_out));
  Multiplexer #(.select(4), .width(32), .enable("false")) multiplexer_2 (
    .in0(ALU_ADD), .in1(ALU_MULT), .in2(ALU_SUB), .in3(ALU_SLL), .in4(ALU_MULH), .in5(ALU_MULHU),
    .in6(ALU_XOR), .in7(ALU_DIV), .in8(ALU_DIVU), .in9(ALU_SRL), .in10(ALU_OR), .in11(ALU_REMU),
    .in12(ALU_AND), .in13(ALU_SLT), .in14(B), .in15(ALU_SRA), .out(Result), .sel(ALUSel));
  Multiplexer #(.width(32), .enable("false")) multiplexer_3 (
    .in0(B), .in1(negator_2_out), .out(multiplexer_3_out), .sel(B[31]));
  Multiplexer #(.width(32), .enable("false")) multiplexer_4 (
    .in0(A), .in1(negator_3_out), .out(multiplexer_4_out), .sel(A[31]));
  Multiplier #(.width(32)) multiplier_2 (
    .a(multiplexer_1_out), .b(multiplexer_3_out), .out(LOW32), .cout(multiplier_2_cout));  // open: cin
  xor xor_2 (xor_2_out, A[31], B[31]);
  Multiplexer #(.width(32), .enable("false")) multiplexer_5 (
    .in0(B), .in1(negator_4_out), .out(multiplexer_5_out), .sel(B[31]));
  assign not_1_out = ~multiplier_2_cout;  // NOT_Gate not_1, 32 bits wide
  Divider #(.width(32)) divider_2 (
    .a(multiplexer_4_out), .b(multiplexer_5_out), .out(divider_2_out));  // open: upper, rem
  xor xor_3 (xor_3_out, A[31], B[31]);
  assign not_2_out = ~LOW32;  // NOT_Gate not_2, 32 bits wide
  assign bit_extender_7_out = {{31{1'b0}}, C_out};  // Bit_Extender bit_extender_7
  Negator #(.width(32)) negator_5 (.in(divider_2_out), .out(negator_5_out));
  Adder #(.width(32)) adder_3 (.a(32'h1), .b(not_2_out), .cout(C_out));  // open: out, cin
  Multiplexer #(.width(32), .enable("false")) multiplexer_6 (
    .in0(multiplier_2_cout), .in1(adder_4_out), .out(ALU_MULH), .sel(xor_2_out));
  Adder #(.width(32)) adder_4 (.a(not_1_out), .b(bit_extender_7_out), .out(adder_4_out));  // open: cin, cout
  Multiplexer #(.width(32), .enable("false")) multiplexer_7 (
    .in0(divider_2_out), .in1(negator_5_out), .out(ALU_DIV), .sel(xor_3_out));

  // Notes on the sheet:
  //   INPUTS to your circuit
  //   OUTPUT from your circuit
  //   DON'T CHANGE THE LOCATIONS OF THE INPUTS AND OUTPUTS!
endmodule
