// Logisim project cpu.circ as structural Verilog: 4 circuits, main circuit main
module main (
  input  [31:0] INSTRUCTION,
  input  CLOCK,
  output [31:0] FETCH_ADDRESS,
  output [31:0] ra,
  output [31:0] sp,
  output [31:0] t0,
  output [31:0] t1,
  output [31:0] t2,
  output [31:0] s0,
  output [31:0] s1,
  output [31:0] a0
);

  wire ASel, AUIPC, BrEq, BrLT, BrUn, BSel, Load_Byte, Load_Half, Load_Un, MemRW, PCSel, RegWEn;
  wire [1:0] Load_type, multiplexer_5_out, WBSel;
  wire [2:0] ImmSel;
  wire [3:0] ALUSel;
  wire [31:0] adder_1_out, adder_2_out, ALU_result, bit_extender_1_out, bit_extender_2_out,
       bit_extender_3_out, bit_extender_4_out, DataA, DataB, DMEM_readdata, Immx, inst, mem,
       multiplexer_1_out, multiplexer_6_out, multiplexer_8_out, multiplexer_9_out, multiplexer_10_out,
       multiplexer_11_out, multiplexer_13_out, PC_D, Real_DataA, Real_Imm, Real_PC_D, shifter_1_out,
       shifter_2_out, shifter_3_out, shifter_4_out, wb;

  Shifter #(.width(32), .shift("ar")) shifter_1 (.in(DataA), .\dist (5'b00010), .out(shifter_1_out));
  Shifter #(.width(32)) shifter_2 (.in(PC_D), .\dist (5'b00010), .out(shifter_2_out));
  Shifter #(.width(32), .shift("ar")) shifter_3 (.in(Immx), .\dist (5'b00010), .out(shifter_3_out));
  Multiplexer #(.width(32), .enable("false")) multiplexer_1 (
    .in0(adder_1_out), .in1(ALU_result), .out(multiplexer_1_out), .sel(PCSel));
  Multiplexer #(.width(32), .enable("false")) multiplexer_2 (
    .in0(DataA), .in1(shifter_1_out), .out(Real_DataA), .sel(PCSel));
  Multiplexer #(.width(32), .enable("false")) multiplexer_3 (
    .in0(PC_D), .in1(shifter_2_out), .out(Real_PC_D), .sel(AUIPC));
  Multiplexer #(.width(32), .enable("false")) multiplexer_4 (
    .in0(Immx), .in1(shifter_3_out), .out(Real_Imm), .sel(PCSel));
  Multiplexer #(.width(2), .enable("false")) multiplexer_5 (
    .in0(2'b10), .in1(2'b00), .out(multiplexer_5_out), .sel(Load_Byte));
  Register #(.width(32)) register_1 (.D(multiplexer_1_out), .clk(CLOCK), .Q(FETCH_ADDRESS));  // open: en, clr
  mem_main DMEM (.WriteAddr(ALU_result), .WriteData(DataB), .MemRW(MemRW), .ReadData(DMEM_readdata), .clk(CLOCK));
  Multiplexer #(.width(32), .enable("false")) multiplexer_6 (
    .in0(INSTRUCTION), .in1(32'h13), .out(multiplexer_6_out), .sel(PCSel));
  Multiplexer #(.width(2), .enable("false")) multiplexer_7 (
    .in0(multiplexer_5_out), .in1(2'b01), .out(Load_type), .sel(Load_Half));
  Adder #(.width(32)) adder_1 (.a(32'h1), .b(FETCH_ADDRESS), .out(adder_1_out));  // open: cin, cout
  Register #(.width(32)) register_2 (.D(FETCH_ADDRESS), .clk(CLOCK), .Q(PC_D));  // open: en, clr
  Register #(.width(32)) register_3 (.D(multiplexer_6_out), .clk(CLOCK), .Q(inst));  // open: en, clr
  assign bit_extender_1_out = {{24{DMEM_readdata[7]}}, DMEM_readdata[7:0]};  // Bit_Extender bit_extender_1
  assign bit_extender_2_out = {{24{1'b0}}, DMEM_readdata[7:0]};  // Bit_Extender bit_extender_2
  assign bit_extender_3_out = {{16{DMEM_readdata[15]}}, DMEM_readdata[15:0]};  // Bit_Extender bit_extender_3
  assign bit_extender_4_out = {{16{1'b0}}, DMEM_readdata[15:0]};  // Bit_Extender bit_extender_4
  Multiplexer #(.width(32), .enable("false")) multiplexer_8 (
    .in0(bit_extender_1_out), .in1(bit_extender_2_out), .out(multiplexer_8_out), .sel(Load_Un));
  Multiplexer #(.width(32), .enable("false")) multiplexer_9 (
    .in0(bit_extender_3_out), .in1(bit_extender_4_out), .out(multiplexer_9_out), .sel(Load_Un));
  Multiplexer #(.width(32), .enable("false")) multiplexer_10 (
    .in0(Real_DataA), .in1(Real_PC_D), .out(multiplexer_10_out), .sel(ASel));
  Multiplexer #(.width(32), .enable("false")) multiplexer_11 (
    .in0(DataB), .in1(Real_Imm), .out(multiplexer_11_out), .sel(BSel));
  Multiplexer #(.select(2), .width(32), .enable("false")) multiplexer_12 (
    .in0(multiplexer_8_out), .in1(multiplexer_9_out), .in2(DMEM_readdata), .out(mem), .sel(Load_type));  // open: in3
  Branch_Comp branch_comp_1 (.BrEq(BrEq), .BrLT(BrLT), .DataA(DataA), .DataB(DataB), .BrUn(BrUn));
  alu Arithmetic_Logic_Unit (.A(multiplexer_10_out), .B(multiplexer_11_out), .ALUSel(ALUSel), .Result(ALU_result));
  Adder #(.width(32)) adder_2 (.a(PC_D), .b(32'h1), .out(adder_2_out));  // open: cin, cout
  Multiplexer #(.select(2), .width(32), .enable("false")) multiplexer_13 (
    .in0(mem), .in1(ALU_result), .in2(adder_2_out), .out(multiplexer_13_out), .sel(WBSel));  // open: in3
  Imm_Gen imm_gen_1 (.Immediate(Immx), .Instruction(inst), .Imm_Sel(ImmSel));
  regfile_main RegFile (
    .rs2(inst[24:20]), .rd(inst[11:7]), .Read_Data_1(DataA), .Read_Data_2(DataB), .ra(ra), .sp(sp), .t0(t0),
    .t1(t1), .t2(t2), .s0(s0), .s1(s1), .a0(a0), .rs1(inst[19:15]), .Write_Data(wb), .RegWEn(RegWEn),
    .clk(CLOCK));
  Shifter #(.width(32)) shifter_4 (.in(multiplexer_13_out), .\dist (5'b00010), .out(shifter_4_out));
  Control control_1 (
    .Instruction(inst), .BrEq(BrEq), .BrLT(BrLT), .PCSel(PCSel), .ImmSel(ImmSel), .BrUn(BrUn), .ASel(ASel),
    .BSel(BSel), .ALUSel(ALUSel), .MemRW(MemRW), .RegWEn(RegWEn), .WBSel(WBSel), .Load_Byte(Load_Byte),
    .Load_Half(Load_Half), .Load_Un(Load_Un), .AUIPC(AUIPC));
  Multiplexer #(.width(32), .enable("false")) multiplexer_14 (
    .in0(multiplexer_13_out), .in1(shifter_4_out), .out(wb), .sel(PCSel));

  // Other names for the same wires on the sheet: clk = CLOCK; fetch_addr[31:0] = FETCH_ADDRESS

  // Notes on the sheet:
  //   Output
  //   Inputs/Outputs from run.circ. DO NOT MOVE THESE.
  //   Inputs
  //   Instruction Fetch
  //   Memory
  //   Load _byte
  //   Load_half
  //   Load_word
  //   Execution
  //   Inputs/Outputs from run.circ. DO NOT MOVE THESE.
  //   Instruction Decode
  //   Write Back
  //   Control Module
endmodule

module Branch_Comp (
  input  [31:0] DataA,
  input  [31:0] DataB,
  input  BrUn,
  output BrEq,
  output BrLT
);

  wire comparator_1_eq, comparator_1_lt, comparator_2_eq, comparator_2_lt;

  Comparator #(.width(32)) comparator_1 (.a(DataA), .b(DataB), .eq(comparator_1_eq), .lt(comparator_1_lt));  // open: gt
  Comparator #(.width(32), .mode("unsigned")) comparator_2 (
    .a(DataA), .b(DataB), .eq(comparator_2_eq), .lt(comparator_2_lt));  // open: gt
  Multiplexer multiplexer_1 (.in0(comparator_1_eq), .in1(comparator_2_eq), .out(BrEq), .sel(BrUn));  // open: en
  Multiplexer multiplexer_2 (.in0(comparator_1_lt), .in1(comparator_2_lt), .out(BrLT), .sel(BrUn));  // open: en
endmodule

module Imm_Gen (
  input  [31:0] Instruction,
  input  [2:0] Imm_Sel,
  output [31:0] Immediate
);

  wire [11:0] bit_extender_1_out;
  wire [31:0] bit_extender_2_out, bit_extender_3_out, bit_extender_4_out, bit_extender_5_out;

  assign bit_extender_1_out = {{11{1'b0}}, 1'b0};  // Bit_Extender bit_extender_1
  assign bit_extender_2_out = {{20{Instruction[31]}}, Instruction[31:20]};  // Bit_Extender bit_extender_2
  assign bit_extender_3_out = {{20{Instruction[31]}}, {Instruction[31:25], Instruction[11:7]}};  // Bit_Extender bit_extender_3
  assign bit_extender_4_out = {{19{Instruction[31]}}, {Instruction[31], Instruction[7], Instruction[30:25], Instruction[11:8], 1'b0}};  // Bit_Extender bit_extender_4
  assign bit_extender_5_out = {{11{Instruction[31]}}, {Instruction[31], Instruction[19:12], Instruction[20], Instruction[30:21], 1'b0}};  // Bit_Extender bit_extender_5
  Multiplexer #(.select(3), .width(32)) multiplexer_1 (
    .in0(bit_extender_2_out), .in1(bit_extender_3_out), .in2(bit_extender_4_out),
    .in3({Instruction[31:12], bit_extender_1_out}), .in4(bit_extender_5_out), .out(Immediate), .sel(Imm_Sel));  // open: in5, in6, in7, en

  // Notes on the sheet:
  //   I
  //   S
  //   B
  //   U
  //   J
endmodule

module Control (
  input  [31:0] Instruction,
  input  BrEq,
  input  BrLT,
  output PCSel,
  output [2:0] ImmSel,
  output BrUn,
  output ASel,
  output BSel,
  output [3:0] ALUSel,
  output MemRW,
  output RegWEn,
  output [1:0] WBSel,
  output Load_Byte,
  output Load_Half,
  output Load_Un,
  output AUIPC
);

  wire and_1_out, and_2_out, and_3_out, and_4_out, and_5_out, B_BEQ, B_BGEU, B_BLT, B_BLTU, B_BNE, B_type,
       Branch_taken, FC3_is_0, FC3_is_1, FC3_is_2, FC3_is_3, FC3_is_4, FC3_is_5, FC3_is_6, FC3_is_7,
       FC7_is_00, FC7_is_01, FC7_is_20, I, I_ADDI, I_ANDI, I_LB, I_LBU, I_LH, I_LHU, I_LW, I_ORI, I_SLLI,
       I_SLTI, I_SRAI, I_SRLI, I_type, I_type_Load, I_XORI, JAL, JALR, LUI, not_1_out, not_2_out, or_3_out,
       or_6_out, or_9_out, or_11_out, or_12_out, or_13_out, or_14_out, or_16_out, R_ADD, R_AND, R_DIV,
       R_DIVU, R_MUL, R_MULH, R_MULHU, R_OR, R_REMU, R_SLL, R_SRL, R_SUB, R_type, R_XOR, U;
  wire [1:0] multiplexer_9_out, multiplexer_14_out;
  wire [2:0] multiplexer_11_out, multiplexer_13_out, multiplexer_15_out, multiplexer_17_out;
  wire [3:0] multiplexer_1_out, multiplexer_2_out, multiplexer_3_out, multiplexer_4_out, multiplexer_5_out,
       multiplexer_6_out, multiplexer_7_out, multiplexer_8_out, multiplexer_10_out, multiplexer_12_out,
       multiplexer_16_out, multiplexer_19_out, multiplexer_21_out, multiplexer_22_out, multiplexer_23_out;

  not not_1 (not_1_out, BrEq);
  not not_2 (not_2_out, BrLT);
  and and_1 (and_1_out, B_BEQ, BrEq);
  and and_2 (and_2_out, B_BNE, not_1_out);
  and and_3 (and_3_out, B_BLT, BrLT);
  and and_4 (and_4_out, B_BLTU, BrLT);
  and and_5 (and_5_out, B_BGEU, not_2_out);
  or or_1 (ASel, B_type, AUIPC, JAL);
  or or_2 (Load_Byte, I_LB, I_LBU);
  Multiplexer #(.width(4), .enable("false")) multiplexer_1 (
    .in0(4'b0000), .in1(4'b0000), .out(multiplexer_1_out), .sel(or_3_out));
  or or_3 (or_3_out, B_type, AUIPC, R_ADD, I_ADDI, I_type_Load, JALR, JAL, MemRW);
  Multiplexer #(.width(4), .enable("false")) multiplexer_2 (
    .in0(multiplexer_1_out), .in1(4'b0001), .out(multiplexer_2_out), .sel(R_MUL));
  Demultiplexer #(.select(3), .enable("false")) demultiplexer_1 (
    .out0(FC3_is_0), .out1(FC3_is_1), .out2(FC3_is_2), .out3(FC3_is_3), .out4(FC3_is_4), .out5(FC3_is_5),
    .out6(FC3_is_6), .out7(FC3_is_7), .in(1'b1), .sel(Instruction[14:12]));
  or or_4 (Branch_taken, and_1_out, and_2_out, and_3_out, and_4_out, and_5_out);
  or or_5 (Load_Half, I_LH, I_LHU);
  Multiplexer #(.width(4), .enable("false")) multiplexer_3 (
    .in0(multiplexer_2_out), .in1(4'b0010), .out(multiplexer_3_out), .sel(R_SUB));
  not not_3 (BSel, R_type);
  Multiplexer #(.width(4), .enable("false")) multiplexer_4 (
    .in0(multiplexer_3_out), .in1(4'b0011), .out(multiplexer_4_out), .sel(or_6_out));
  or or_6 (or_6_out, R_SLL, I_SLLI);
  Multiplexer #(.width(4), .enable("false")) multiplexer_5 (
    .in0(multiplexer_4_out), .in1(4'b0100), .out(multiplexer_5_out), .sel(R_MULH));
  Comparator #(.width(7)) comparator_1 (.a(Instruction[6:0]), .b(7'b0110011), .eq(R_type));  // open: gt, lt
  Comparator #(.width(7)) comparator_2 (.a(Instruction[6:0]), .b(7'b0000011), .eq(I_type_Load));  // open: gt, lt
  Comparator #(.width(7)) comparator_3 (.a(Instruction[6:0]), .b(7'b0010011), .eq(I_type));  // open: gt, lt
  Comparator #(.width(7)) comparator_4 (.a(Instruction[6:0]), .b(7'b0100011), .eq(MemRW));  // open: gt, lt
  Comparator #(.width(7)) comparator_5 (.a(Instruction[6:0]), .b(7'b1100011), .eq(B_type));  // open: gt, lt
  Comparator #(.width(7)) comparator_6 (.a(Instruction[6:0]), .b(7'b0010111), .eq(AUIPC));  // open: gt, lt
  Comparator #(.width(7)) comparator_7 (.a(Instruction[6:0]), .b(7'b0110111), .eq(LUI));  // open: gt, lt
  Comparator #(.width(7)) comparator_8 (.a(Instruction[6:0]), .b(7'b1101111), .eq(JAL));  // open: gt, lt
  Comparator #(.width(7)) comparator_9 (.a(Instruction[6:0]), .b(7'b1100111), .eq(JALR));  // open: gt, lt
  Comparator #(.width(7)) comparator_10 (.a(Instruction[31:25]), .b({7{1'b0}}), .eq(FC7_is_00));  // open: gt, lt
  Comparator #(.width(7)) comparator_11 (.a(Instruction[31:25]), .b(7'b0000001), .eq(FC7_is_01));  // open: gt, lt
  Comparator #(.width(7)) comparator_12 (.a(Instruction[31:25]), .b(7'b0100000), .eq(FC7_is_20));  // open: gt, lt
  or or_7 (PCSel, JAL, JALR, Branch_taken);
  or or_8 (Load_Un, I_LBU, I_LHU);
  Multiplexer #(.width(4), .enable("false")) multiplexer_6 (
    .in0(multiplexer_5_out), .in1(4'b0101), .out(multiplexer_6_out), .sel(R_MULHU));
  Multiplexer #(.width(4), .enable("false")) multiplexer_7 (
    .in0(multiplexer_6_out), .in1(4'b0110), .out(multiplexer_7_out), .sel(or_9_out));
  or or_9 (or_9_out, R_XOR, I_XORI);
  Multiplexer #(.width(4), .enable("false")) multiplexer_8 (
    .in0(multiplexer_7_out), .in1(4'b0111), .out(multiplexer_8_out), .sel(R_DIV));
  Multiplexer #(.width(2), .enable("false")) multiplexer_9 (
    .in0(2'b00), .in1(2'b00), .out(multiplexer_9_out), .sel(I_type_Load));
  Multiplexer #(.width(4), .enable("false")) multiplexer_10 (
    .in0(multiplexer_8_out), .in1(4'b1000), .out(multiplexer_10_out), .sel(R_DIVU));
  or or_10 (I, I_type_Load, JALR, I_type);
  Multiplexer #(.width(3), .enable("false")) multiplexer_11 (
    .in0(3'b000), .in1(3'b000), .out(multiplexer_11_out), .sel(I));
  or or_11 (or_11_out, I_type, R_type, AUIPC, LUI);
  Multiplexer #(.width(4), .enable("false")) multiplexer_12 (
    .in0(multiplexer_10_out), .in1(4'b1001), .out(multiplexer_12_out), .sel(or_12_out));
  or or_12 (or_12_out, R_SRL, I_SRLI);
  and and_6 (R_ADD, R_type, FC3_is_0, FC7_is_00);
  and and_7 (R_MUL, R_type, FC3_is_0, FC7_is_01);
  and and_8 (R_SUB, R_type, FC3_is_0, FC7_is_20);
  and and_9 (R_SLL, R_type, FC3_is_1, FC7_is_00);
  and and_10 (R_MULH, R_type, FC3_is_1, FC7_is_01);
  and and_11 (R_MULHU, R_type, FC3_is_3, FC7_is_01);
  and and_12 (R_XOR, R_type, FC3_is_4, FC7_is_00);
  and and_13 (R_DIV, R_type, FC3_is_4, FC7_is_01);
  and and_14 (R_DIVU, R_type, FC3_is_5, FC7_is_01);
  and and_15 (R_SRL, R_type, FC3_is_5, FC7_is_00);
  and and_16 (R_OR, R_type, FC3_is_6, FC7_is_00);
  and and_17 (R_REMU, R_type, FC3_is_7, FC7_is_01);
  and and_18 (R_AND, R_type, FC3_is_7, FC7_is_00);
  and and_19 (B_BLT, B_type, FC3_is_4);
  and and_20 (B_BLTU, B_type, FC3_is_6);
  Multiplexer #(.width(3), .enable("false")) multiplexer_13 (
    .in0(multiplexer_11_out), .in1(3'b001), .out(multiplexer_13_out), .sel(MemRW));
  Multiplexer #(.width(2), .enable("false")) multiplexer_14 (
    .in0(multiplexer_9_out), .in1(2'b01), .out(multiplexer_14_out), .sel(or_11_out));
  or or_13 (or_13_out, R_OR, I_ORI);
  Multiplexer #(.width(3), .enable("false")) multiplexer_15 (
    .in0(multiplexer_13_out), .in1(3'b010), .out(multiplexer_15_out), .sel(B_type));
  or or_14 (or_14_out, JALR, JAL);
  Multiplexer #(.width(4), .enable("false")) multiplexer_16 (
    .in0(multiplexer_12_out), .in1(4'b1010), .out(multiplexer_16_out), .sel(or_13_out));
  Multiplexer #(.width(3), .enable("false")) multiplexer_17 (
    .in0(multiplexer_15_out), .in1(3'b011), .out(multiplexer_17_out), .sel(U));
  Multiplexer #(.width(2), .enable("false")) multiplexer_18 (
    .in0(multiplexer_14_out), .in1(2'b10), .out(WBSel), .sel(or_14_out));
  Multiplexer #(.width(4), .enable("false")) multiplexer_19 (
    .in0(multiplexer_16_out), .in1(4'b1011), .out(multiplexer_19_out), .sel(R_REMU));
  or or_15 (U, AUIPC, LUI);
  Multiplexer #(.width(3), .enable("false")) multiplexer_20 (
    .in0(multiplexer_17_out), .in1(3'b100), .out(ImmSel), .sel(JAL));
  Multiplexer #(.width(4), .enable("false")) multiplexer_21 (
    .in0(multiplexer_19_out), .in1(4'b1100), .out(multiplexer_21_out), .sel(or_16_out));
  or or_16 (or_16_out, R_AND, I_ANDI);
  Multiplexer #(.width(4), .enable("false")) multiplexer_22 (
    .in0(multiplexer_21_out), .in1(4'b1101), .out(multiplexer_22_out), .sel(I_SLTI));
  and and_21 (I_LB, I_type_Load, FC3_is_0);
  and and_22 (I_LH, I_type_Load, FC3_is_1);
  and and_23 (I_LW, I_type_Load, FC3_is_2);
  and and_24 (I_LBU, I_type_Load, FC3_is_4);
  and and_25 (I_LHU, I_type_Load, FC3_is_5);
  and and_26 (I_ADDI, I_type, FC3_is_0);
  and and_27 (I_SLLI, I_type, FC3_is_1, FC7_is_00);
  and and_28 (I_SLTI, I_type, FC3_is_2);
  and and_29 (I_XORI, I_type, FC3_is_4);
  and and_30 (I_SRLI, I_type, FC3_is_5, FC7_is_00);
  and and_31 (I_ORI, I_type, FC3_is_6);
  and and_32 (I_ANDI, I_type, FC3_is_7);
  and and_33 (B_BEQ, B_type, FC3_is_0);
  and and_34 (B_BNE, B_type, FC3_is_1);
  and and_35 (B_BGEU, B_type, FC3_is_7);
  nor nor_1 (RegWEn, MemRW, B_type);
  Multiplexer #(.width(4), .enable("false")) multiplexer_23 (
    .in0(multiplexer_22_out), .in1(4'b1110), .out(multiplexer_23_out), .sel(LUI));
  or or_17 (BrUn, B_BLTU, B_BGEU);
  Multiplexer #(.width(4), .enable("false")) multiplexer_24 (
    .in0(multiplexer_23_out), .in1(4'b1111), .out(ALUSel), .sel(I_SRAI));
  and and_36 (I_SRAI, I_type, FC3_is_5, FC7_is_20);

  // Other names for the same wires on the sheet: opcode[6:0] = Instruction[6:0]; func3[2:0] = Instruction[14:12];
  //   func7[6:0] = Instruction[31:25]; SW = MemRW

  // Notes on the sheet:
  //   Input
  //   Output
  //   ASel
  //   PCSel
  //   Judge Load Type
  //   BSel
  //   Extract Feature
  //   Judge Type
  //   Judge func3 and func7
  //   MemRW
  //   ALUSel
  //   WBSel
  //   ImmSel
  //   Judge Instruction
  //   RegWEn
  //   BrUn
endmodule
